// Logisim project Exercício - 2.circ as structural Verilog: 1 circuit, main circuit main
module main (
  input  in_1,
  input  in_2,
  input  in_3,
  input  in_4,
  input  in_5,
  input  in_6,
  input  in_7,
  input  in_8,
  input  in_9,
  input  in_10,
  input  in_11
);

  wire and_1_out, and_2_out, and_3_out, and_4_out, and_5_out, or_1_out, or_2_out;

  and and_1 (and_1_out, in_1, in_3);
  and and_2 (and_2_out, in_5, in_7);
  and and_3 (and_3_out, in_9, in_11);
  or or_1 (or_1_out, and_1_out, and_2_out, and_3_out);
  LED led_1 (.in(or_1_out));
  and and_4 (and_4_out, in_2, in_4, in_6);
  and and_5 (and_5_out, in_8, in_10);
  LED led_2 (.in(or_2_out));
  or or_2 (or_2_out, and_4_out, and_5_out);

  // Notes on the sheet:
  //   Exercicio
endmodule
